# Fritzing sketch FruitMachine (saved by Fritzing 0.9.4)
perfboards: 1

parts:
  Mod5 = KY-010 Photo Interrupter Module [package="Breakout board"]
  M1 = Stepper Motor - Unipolar
  LED1 = LED - 5mm [color="White (4500K)" package="5 mm [THT]"]
  LED2 = LED - 5mm [color="White (4500K)" package="5 mm [THT]"]
  LED3 = LED - 5mm [color="White (4500K)" package="5 mm [THT]"]
  J1 = female pin header, 15 pins [form="♀ (female)"]
  Part1 = RAMPS 1.4 Shield for Arduino Mega 2560
  M2 = Stepper Motor - Unipolar
  LED4 = LED - 5mm [color="White (4500K)" package="5 mm [THT]"]
  LED5 = LED - 5mm [color="White (4500K)" package="5 mm [THT]"]
  LED6 = LED - 5mm [color="White (4500K)" package="5 mm [THT]"]
  J2 = female pin header, 15 pins [form="♀ (female)"]
  Mod6 = KY-010 Photo Interrupter Module [package="Breakout board"]
  M3 = Stepper Motor - Unipolar
  M4 = Stepper Motor - Unipolar
  LED7 = LED - 5mm [color="White (4500K)" package="5 mm [THT]"]
  LED8 = LED - 5mm [color="White (4500K)" package="5 mm [THT]"]
  LED9 = LED - 5mm [color="White (4500K)" package="5 mm [THT]"]
  LED10 = LED - 5mm [color="White (4500K)" package="5 mm [THT]"]
  LED11 = LED - 5mm [color="White (4500K)" package="5 mm [THT]"]
  LED12 = LED - 5mm [color="White (4500K)" package="5 mm [THT]"]
  J3 = female pin header, 15 pins [form="♀ (female)"]
  J4 = female pin header, 15 pins [form="♀ (female)"]
  Mod7 = KY-010 Photo Interrupter Module [package="Breakout board"]
  Mod8 = KY-010 Photo Interrupter Module [package="Breakout board"]
  WeMos_D1_Mini1 = WeMos D1 Mini
  IC6 = IC, DIP package, 20 pins [chip_label=TPIC6B595]
  Shift_Register1 = 74HC595 [package="DIP16 [THT]"]
  8-Channel_Source1 = DIP - 18 pins [package="DIP (Dual Inline) [THT]"]
  J5 = male pin header, 5 pins [form="♂ (male)"]
  J6 = male pin header, 12 pins [form="♂ (male)"]
  J7 = screw terminal, 3 pins
  R1 = Resistor [tolerance=±5% resistance=470 package=THT]
  R2 = Resistor [tolerance=±5% resistance=470 package=THT]
  R3 = Resistor [tolerance=±5% resistance=470 package=THT]
  R4 = Resistor [tolerance=±5% resistance=470 package=THT]
  R5 = Resistor [tolerance=±5% resistance=470 package=THT]
  R6 = Resistor [tolerance=±5% resistance=470 package=THT]
  R7 = Resistor [tolerance=±5% resistance=470 package=THT]
  R8 = Resistor [tolerance=±5% resistance=680 package=THT]
  C1 = Ceramic Capacitor [capacitance=100nF package="100 mil [THT, multilayer]"]
  C2 = Ceramic Capacitor [capacitance=100nF package="100 mil [THT, multilayer]"]
  S1 = Square Pushbutton
  S2 = Square Pushbutton
  S3 = Square Pushbutton
  S4 = Square Pushbutton
  S5 = Square Pushbutton
  S6 = Square Pushbutton
  S7 = Square Pushbutton
  M5 = fc-51 [package=THT]
  7_Segment1 = 7 Segment Display  # not connected
  7_Segment2 = 7 Segment Display  # not connected
  7_Segment3 = 7 Segment Display  # not connected
  7_Segment4 = 7 Segment Display  # not connected
  SP1 = SPEAKER [package=pcb_mount_speaker]  # not connected
  LED13 = LED - 5mm [color="Yellow (595nm)" package="5 mm [THT]"]  # not connected
  LED14 = LED - 5mm [color="Yellow (595nm)" package="5 mm [THT]"]  # not connected
  LED15 = LED - 5mm [color="Yellow (595nm)" package="5 mm [THT]"]  # not connected
  LED16 = LED - 5mm [color="Yellow (595nm)" package="5 mm [THT]"]  # not connected
  LED17 = LED - 5mm [color="Yellow (595nm)" package="5 mm [THT]"]  # not connected
  LED18 = LED - 5mm [color="Yellow (595nm)" package="5 mm [THT]"]  # not connected
  LED19 = LED - 5mm [color="Yellow (595nm)" package="5 mm [THT]"]  # not connected
  LED20 = LED - 5mm [color="Yellow (595nm)" package="5 mm [THT]"]  # not connected
  LED21 = LED - 5mm [color="Yellow (595nm)" package="5 mm [THT]"]  # not connected
  LED22 = LED - 5mm [color="Yellow (595nm)" package="5 mm [THT]"]  # not connected
  LED23 = LED - 5mm [color="Yellow (595nm)" package="5 mm [THT]"]  # not connected
  LED24 = LED - 5mm [color="Yellow (595nm)" package="5 mm [THT]"]  # not connected
  LED25 = LED - 5mm [color="Yellow (595nm)" package="5 mm [THT]"]  # not connected
  LED26 = LED - 5mm [color="Yellow (595nm)" package="5 mm [THT]"]  # not connected
  LED27 = LED - 5mm [color="Yellow (595nm)" package="5 mm [THT]"]  # not connected
  LED28 = LED - 5mm [color="Yellow (595nm)" package="5 mm [THT]"]  # not connected
  LED29 = LED - 5mm [color="Yellow (595nm)" package="5 mm [THT]"]  # not connected
  LED30 = LED - 5mm [color="Yellow (595nm)" package="5 mm [THT]"]  # not connected
  MP3-1 = Serial MP3 Player

nets:
  N1: Mod5.-, J1.pin11, Part1.GND/XMIN_ENDSTOP
  N2: Mod5.Vin, J1.pin8, J1.pin9, Part1.5V/XMIN_ENDSTOP
  N3: Mod5.S, J1.pin10, Part1.D3/XMIN_ENDSTOP
  N4: M1.A, J1.pin3, Part1.X_2B
  N5: M1.COMMON_1, J1.pin1
  N6: M1.C, J1.pin4, Part1.X_2A
  N7: M1.B, J1.pin5, Part1.X_1A
  N8: M1.COMMON_2, J1.pin2
  N9: M1.D, J1.pin6, J1.pin7, Part1.X_1B
  N10: LED1.cathode, LED2.cathode, LED3.cathode, J1.pin15, Part1.D8-, LED4.cathode, LED5.cathode, LED6.cathode, J2.pin15, LED7.cathode, LED8.cathode, LED9.cathode, LED10.cathode, LED11.cathode, LED12.cathode, J3.pin15, J4.pin15
  N11: LED1.anode, J1.pin12
  N12: LED2.anode, J1.pin13, Part1.D8+, LED5.anode, J2.pin13, LED9.anode, LED10.anode, J3.pin13, J4.pin13
  N13: LED3.anode, J1.pin14
  N14: Part1.D63/A9, S1.leg0
  N15: Part1.D64/A10, S4.leg0
  N16: Part1.D65/A11, M5.pin1
  N17: Part1.D66/A12, S7.leg0
  N18: Part1.5V/AUX1A, MP3-1.pin2
  N19: Part1.5V/AUX2, M5.pin3
  N20: Part1.D57/A3, MP3-1.pin3
  N21: Part1.D58/A4, MP3-1.pin4
  N22: Part1.D59/A5, S2.leg0
  N23: Part1.D19/ZMAX_ENDSTOP, WeMos_D1_Mini1.TX
  N24: Part1.D18/ZMIN_ENDSTOP, WeMos_D1_Mini1.RX
  N25: Part1.D15/YMAX_ENDSTOP, J4.pin10, Mod8.S
  N26: Part1.D14/YMIN_ENDSTOP, J3.pin10, Mod7.S
  N27: Part1.GND/AUX1A, MP3-1.pin1
  N28: Part1.5V/XMAX_ENDSTOP, J2.pin9, Mod6.Vin
  N29: Part1.5V/YMIN_ENDSTOP, J3.pin8, J3.pin9, Mod7.Vin
  N30: Part1.5V/YMAX_ENDSTOP, J4.pin9, Mod8.Vin
  N31: Part1.5V/ZMIN_ENDSTOP, WeMos_D1_Mini1.5V
  N32: Part1.GND/AUX2, S1.leg1, S2.leg1, S3.leg1, S4.leg1, S5.leg1, S6.leg1, S7.leg1, M5.pin2
  N33: Part1.D40/AUX2, S3.leg0
  N34: Part1.D42/AUX2, S6.leg0
  N35: Part1.D44/AUX2, S5.leg0
  N36: Part1.GND/XMAX_ENDSTOP, J2.pin11, Mod6.-
  N37: Part1.GND/YMIN_ENDSTOP, J3.pin11, Mod7.-
  N38: Part1.GND/YMAX_ENDSTOP, J4.pin11, Mod8.-
  N39: Part1.GND/ZMIN_ENDSTOP, WeMos_D1_Mini1.G
  N40: Part1.D2/XMAX_ENDSTOP, J2.pin10, Mod6.S
  N41: Part1.E0_2B, M4.A, J4.pin3
  N42: Part1.E0_2A, M4.C, J4.pin4
  N43: Part1.E0_1A, M4.B, J4.pin5
  N44: Part1.E0_1B, M4.D, J4.pin6
  N45: Part1.Y_2B, M2.A, J2.pin3
  N46: Part1.Y_2A, M2.C, J2.pin4
  N47: Part1.Y_1A, M2.B, J2.pin5
  N48: Part1.Y_1B, M2.D, J2.pin6
  N49: Part1.Z_BTM_2B, M3.A, J3.pin3
  N50: Part1.Z_BTM_2A, M3.C, J3.pin4
  N51: Part1.Z_BTM_1A, M3.B, J3.pin5
  N52: Part1.Z_BTM_1B, M3.D, J3.pin6, J3.pin7
  N53: M2.COMMON_1, J2.pin1
  N54: M2.COMMON_2, J2.pin2
  N55: LED4.anode, J2.pin14
  N56: LED6.anode, J2.pin12
  N57: M3.COMMON_1, J3.pin1
  N58: M3.COMMON_2, J3.pin2
  N59: M4.COMMON_1, J4.pin1
  N60: M4.COMMON_2, J4.pin2
  N61: LED7.anode, J3.pin14
  N62: LED8.anode, J4.pin14
  N63: LED11.anode, J3.pin12
  N64: LED12.anode, J4.pin12
  N65: IC6.pin2, IC6.pin8, Shift_Register1.MR, Shift_Register1.VCC, J5.pin5, C1.1, C2.1
  N66: IC6.pin3, Shift_Register1.Q7'
  N67: IC6.pin4, R1.Pin_0
  N68: IC6.pin5, R2.Pin_0
  N69: IC6.pin6, R3.Pin_0
  N70: IC6.pin7, R4.Pin_0
  N71: IC6.pin9, IC6.pin10, IC6.pin11, IC6.pin19, 8-Channel_Source1.GND, J7.pin3, C1.0
  N72: IC6.pin12, Shift_Register1.ST_CP, J5.pin3
  N73: IC6.pin13, Shift_Register1.SH_CP, J5.pin4
  N74: IC6.pin14, R6.Pin_0
  N75: IC6.pin15, R5.Pin_0
  N76: IC6.pin16, R7.Pin_0
  N77: IC6.pin17, R8.Pin_0
  N78: Shift_Register1.Q1, 8-Channel_Source1.In_2
  N79: Shift_Register1.Q2, 8-Channel_Source1.In_3
  N80: Shift_Register1.Q3, 8-Channel_Source1.In_4
  N81: Shift_Register1.GND, Shift_Register1.OE, J5.pin2, C2.0
  N82: Shift_Register1.DS, J5.pin1
  N83: Shift_Register1.Q0, 8-Channel_Source1.In_1
  N84: 8-Channel_Source1.Out_4, J6.pin4
  N85: 8-Channel_Source1.Out_3, J6.pin3
  N86: 8-Channel_Source1.Out_2, J6.pin2
  N87: 8-Channel_Source1.Out_1, J6.pin1
  N88: J6.pin5, R1.Pin_1
  N89: J6.pin6, R2.Pin_1
  N90: J6.pin7, R3.Pin_1
  N91: J6.pin8, R4.Pin_1
  N92: J6.pin9, R6.Pin_1
  N93: J6.pin10, R5.Pin_1
  N94: J6.pin11, R7.Pin_1
  N95: J6.pin12, R8.Pin_1

notes:
  1. Common A (unused) (Green)
  2. Common B (unused) (Green)
  3. A1 (Red)
  4. A2 (Yellow)
  5. B1 (Blue)
  6. B2 (Black)
  7. N/C
  8. N/C
  9. 5V Opto Vin (Pink)
  10. Signal Opto (Brown)
  11. Opto GND (Purple/Blue)
  12. Hi Lamp 12V
  13. Mid Lamp 12V
  14. Low Lamp 12V
  15. GND Lamps
  Opto Sensor out goes HIGH when obstructed
  Reel lamps share a common ground, and separately switched +12V
  Arduino MEGA Serial1 on 19(Rx) and 18(Tx) connected to Wemos D1 to enable Wi-Fi communication
  Opto-sensor to detect coin input would ideally be connected to a GPIO pin with external interrupt (2, 3, 18, 19, 20, 21), but they all have other functions:
  - 2/3 are XMax/XMin endstop
  - 18/19 are ZMin/ZMax endstop (and also Serial1 Rx/Tx)
  - 20/21 are SDA/SCL for I2C interface

custom parts:
  KY-010 Photo Interrupter Module: KY-010 Photo Interrupter Module, it will trigger a signal when light between the sensor's gap is blocked.
  RAMPS 1.4 Shield for Arduino Mega 2560: This ia standard Ramps 1.4 shield which is also compatible with versions 1.5 and 1.6 of the Ramps board. This model is intended only for the breadboard view, as the schematic and PCB views are not entirely accurate.
  DIP - 18 pins: Recommended for high-side switching applications that benefit from separate logic and load grounds, these devices encompass load supply voltages to 50 V and output currents to -500 mA. These 8-channel source drivers are useful for interfacing between low-level logic and high-current loads. Typical loads include relays, solenoids, lamps, stepper and/or servo motors, print hammers, and LEDs.
  Serial MP3 Player: The module is a kind of simple MP3 player device which is based on a high-quality MP3 audio chip---YX5300. It can support 8k Hz ~ 48k Hz sampling frequency MP3 and WAV file formats. There is a TF card socket on board, so you can plug the micro SD card that stores audio files. MCU can control the MP3 playback state by sending commands to the module via UART port, such as switch songs, change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
