# Fritzing sketch FruitMachineLED (saved by Fritzing 0.9.3b)
circuit board: 10cm x 6cm
breadboards: 1

parts:
  Arduino = Arduino Nano (Rev3.0)
  8-Channel_Source = DIP - 18 pins [package="DIP (Dual Inline) [THT]"]
  Shift_Register = 74HC595 [package="DIP16 [THT]"]
  C1 = Ceramic Capacitor [capacitance=100nF package="100 mil [THT, multilayer]"]
  R1 = Resistor [tolerance=±5% resistance=330 package=THT]
  R3 = Resistor [tolerance=±5% resistance=330 package=THT]
  R4 = Resistor [tolerance=±5% resistance=330 package=THT]
  R5 = Resistor [tolerance=±5% resistance=330 package=THT]
  R6 = Resistor [tolerance=±5% resistance=330 package=THT]
  R7 = Resistor [tolerance=±5% resistance=330 package=THT]
  R8 = Resistor [tolerance=±5% resistance=470 package=THT]
  DI2 = 7 Segment Display
  8-Channel_Sink = ULN2803A [package=THT]
  DI3 = 7 Segment Display
  DI4 = 7 Segment Display
  DI5 = 7 Segment Display
  DI6 = 7 Segment Display
  R9 = Resistor [tolerance=±5% resistance=330 package=THT]
  Shift_Register_2 = 74HC595 [package="DIP16 [THT]"]
  C2 = Ceramic Capacitor [capacitance=100nF package="100 mil [THT, multilayer]"]
  IC1 = IC, DIP package, 16 pins [chip_label=CD4094]  # not connected
  IC1_2 = IC, DIP package, 16 pins [chip_label=CD4094]  # not connected

nets:
  GND: Arduino.GND, 8-Channel_Source.GND, Shift_Register.GND, Shift_Register.OE, C1.1, 8-Channel_Sink.0V, Shift_Register_2.GND, Shift_Register_2.OE, C2.1
  N1: Arduino.D8, Shift_Register.ST_CP, Shift_Register_2.ST_CP
  N2: Arduino.D11/MOSI, Shift_Register.DS
  N3: Arduino.D12/MISO, Shift_Register.SH_CP, Shift_Register_2.SH_CP
  VCC: Arduino.5V, Shift_Register.MR, Shift_Register.VCC, C1.0, Shift_Register_2.MR, Shift_Register_2.VCC, C2.0
  N4: 8-Channel_Source.In_1, Shift_Register.Q0
  N5: 8-Channel_Source.In_2, Shift_Register.Q1
  N6: 8-Channel_Source.In_3, Shift_Register.Q2
  N7: 8-Channel_Source.In_4, Shift_Register.Q3
  N8: 8-Channel_Source.In_5, Shift_Register.Q4
  N9: 8-Channel_Source.In_6, Shift_Register.Q5
  N10: 8-Channel_Source.In_7, Shift_Register.Q6
  N11: 8-Channel_Source.In_8, Shift_Register.Q7
  12V: 8-Channel_Source.Vcc
  N12: 8-Channel_Source.Out_8, R8.Pin_0
  N13: 8-Channel_Source.Out_7, R7.Pin_0
  N14: 8-Channel_Source.Out_6, R6.Pin_0
  N15: 8-Channel_Source.Out_5, R5.Pin_0
  N16: 8-Channel_Source.Out_4, R4.Pin_0
  N17: 8-Channel_Source.Out_3, R3.Pin_0
  N18: 8-Channel_Source.Out_2, R1.Pin_0
  N19: 8-Channel_Source.Out_1, R9.Pin_0
  N20: Shift_Register.Q7', Shift_Register_2.DS
  N21: R1.Pin_1, DI2.Segment_B, DI3.Segment_B, DI4.Segment_B, DI5.Segment_B, DI6.Segment_B
  N22: R3.Pin_1, DI2.Segment_C, DI3.Segment_C, DI4.Segment_C, DI5.Segment_C, DI6.Segment_C
  N23: R4.Pin_1, DI2.Segment_D, DI3.Segment_D, DI4.Segment_D, DI5.Segment_D, DI6.Segment_D
  N24: R5.Pin_1, DI2.Segment_E, DI3.Segment_E, DI4.Segment_E, DI5.Segment_E, DI6.Segment_E
  N25: R6.Pin_1, DI2.Segment_F, DI3.Segment_F, DI4.Segment_F, DI5.Segment_F, DI6.Segment_F
  N26: R7.Pin_1, DI2.Segment_G, DI3.Segment_G, DI4.Segment_G, DI5.Segment_G, DI6.Segment_G
  N27: R8.Pin_1, DI2.Segment_DP, DI3.Segment_DP, DI4.Segment_DP, DI5.Segment_DP, DI6.Segment_DP
  N28: DI2.common_cathode, 8-Channel_Sink.Out_4
  N29: DI2.Segment_A, DI3.Segment_A, DI4.Segment_A, DI5.Segment_A, DI6.Segment_A, R9.Pin_1
  N30: 8-Channel_Sink.In_1, Shift_Register_2.Q0
  N31: 8-Channel_Sink.In_2, Shift_Register_2.Q1
  N32: 8-Channel_Sink.In_3, Shift_Register_2.Q2
  N33: 8-Channel_Sink.In_4, Shift_Register_2.Q3
  N34: 8-Channel_Sink.In_5, Shift_Register_2.Q4
  N35: 8-Channel_Sink.In_6, Shift_Register_2.Q5
  N36: 8-Channel_Sink.In_7, Shift_Register_2.Q6
  N37: 8-Channel_Sink.In_8, Shift_Register_2.Q7
  N38: 8-Channel_Sink.Out_8, DI6.common_cathode
  N39: 8-Channel_Sink.Out_7, DI5.common_cathode
  N40: 8-Channel_Sink.Out_6, DI4.common_cathode
  N41: 8-Channel_Sink.Out_5, DI3.common_cathode

notes:
  1.8" FEM-1801L0BGW Common Cathode 7-Segment LEDs
  (http://www.farnell.com/datasheets/99300.pdf)
  Vf = 5.55V, IF = 25 mA
  Pin 8, Green = Latch
  Pin 11, Blue = Data
  Pin 12, Yellow = Clock
  With 12V source, current-limiting resistor required for LED is:
  (12 - 5.5) / 0.025 = 260Ω
  Be conservative with 330Ω on each anode.
  DP has less LEDs so requires greater resistor = 470Ω
  12V DC

custom parts:
  DIP - 18 pins: Recommended for high-side switching applications that benefit from separate logic and load grounds, these devices encompass load supply voltages to 50 V and output currents to -500 mA. These 8-channel source drivers are useful for interfacing between low-level logic and high-current loads. Typical loads include relays, solenoids, lamps, stepper and/or servo motors, print hammers, and LEDs.
