# Fritzing sketch FruitMachineLamps (saved by Fritzing 0.9.3b)
breadboards: 1

parts:
  IC1 = IC, DIP package, 16 pins [chip_label=MIC5891]
  Part1 = Arduino Nano (Rev3.0)
  JACK1 = 2.1mm Barrel Jack with Terminal Block
  LED1 = LEDs [package=led10mm]
  LED2 = LEDs [package=led10mm]
  LED3 = LEDs [package=led10mm]
  LED4 = LEDs [package=led10mm]
  LED5 = LEDs [package=led10mm]
  LED6 = LEDs [package=led10mm]
  LED7 = LEDs [package=led10mm]
  LED8 = LEDs [package=led10mm]

nets:
  N1: IC1.pin1, Part1.GND, JACK1.NEG, LED1.C, LED2.C, LED3.C, LED4.C, LED5.A, LED6.A, LED7.A, LED8.A
  N2: IC1.pin2, Part1.D13/SCK
  N3: IC1.pin3, Part1.D11/MOSI
  N4: IC1.pin4, Part1.D10
  N5: IC1.pin5, LED5.C
  N6: IC1.pin6, LED6.C
  N7: IC1.pin7, LED7.C
  N8: IC1.pin8, LED8.C
  N9: IC1.pin9, LED4.A
  N10: IC1.pin10, LED3.A
  N11: IC1.pin11, LED2.A
  N12: IC1.pin12, LED1.A
  N13: IC1.pin13, JACK1.POS
  N14: IC1.pin14, Part1.D5
  N15: IC1.pin15, Part1.5V

notes:
  The MIC5891 is a high-side 8-channel shift register. It provides equivalent functionality to a 74HC595 and UDN2981 - allowing an Arduino to control a current source <50V@500mA to up to 8 devices via a single serial data in pin. More devices can be daisy-chained together if required. If the OE pin is connected to a PWM-capable pin, the output voltage can be adjusted.
  Arduino MIC5891
  GND GND (Pin 1)
  5V Logic Supply (Pin 15)
  13 Clock (Pin 2)
  11 Serial Data In (Pin 3)
  10 Strobe (Pin 4)
  5 (PWM) Output Enable (Pin 14)
  ---
  12V Load Supply (Pin 13)
  ---
  Lamp +ve Outputs 1-8 (Pins 5-12)
  Pin 16, unused in this example, is the serial data out which can be connected to the serial data in of another MIC5891.
  12V
  The MIC5891 directs this supply to the 8 output channels according to the data data received from the Arduino on the serial in pin

custom parts:
  LEDs: LEDs Standard schematic elements and footprints for 5mm, 3mm, 1206, and 0603 sized LEDs. 5mm - Spark Fun Electronics SKU : COM-00529 (and others)
