# Fritzing sketch FruitMachineReels (saved by Fritzing 0.9.3b)

parts:
  M2 = Stepper Motor - Unipolar
  M3 = Stepper Motor - Unipolar
  M4 = Stepper Motor - Unipolar
  M5 = Stepper Motor - Unipolar
  J1 = male pin header, 10 pins [form="♂ (male)"]
  J2 = male pin header, 22 pins [form="♂ (male)"]
  J3 = male pin header, 23 pins [form="♂ (male)"]
  Part1 = RAMPS 1.4 Shield for Arduino Mega 2560
  Mod1 = KY-010 Photo Interrupter Module [package="Breakout board"]
  Mod2 = KY-010 Photo Interrupter Module [package="Breakout board"]
  Mod3 = KY-010 Photo Interrupter Module [package="Breakout board"]
  Mod4 = KY-010 Photo Interrupter Module [package="Breakout board"]
  IC1 = IC, DIP package, 14 pins [chip_label=TC4093BP]
  LED1 = LED - 5mm [color="Red (633nm)" package="5 mm [THT]"]
  R1 = Resistor [tolerance=±5% resistance=220 package=THT]
  R2 = Resistor [tolerance=±5% resistance=220 package=THT]
  R3 = Resistor [tolerance=±5% resistance=220 package=THT]
  Q1 = PNP-Transistor [package="TO92 [THT]"]
  Mod5 = KY-010 Photo Interrupter Module [package="Breakout board"]  # not connected

nets:
  N1: M2.A, J2.pin4, Part1.X_2B
  N2: M2.COMMON_1, J2.pin2
  N3: M2.C, J2.pin5, Part1.X_2A
  N4: M2.B, J2.pin6, Part1.X_1A
  N5: M2.COMMON_2, J2.pin3
  N6: M2.D, J2.pin7, Part1.X_1B
  N7: M3.A, J2.pin11, Part1.Y_2B
  N8: M3.COMMON_1, J2.pin9
  N9: M3.C, J2.pin12, Part1.Y_2A
  N10: M3.B, J2.pin13, Part1.Y_1A
  N11: M3.COMMON_2, J2.pin10
  N12: M3.D, J2.pin14, Part1.Y_1B
  N13: M4.A, J2.pin19, Part1.Z_BTM_2B
  N14: M4.COMMON_1, J2.pin17
  N15: M4.C, J2.pin20, Part1.Z_BTM_2A
  N16: M4.B, J2.pin21, Part1.Z_BTM_1A
  N17: M4.COMMON_2, J2.pin18
  N18: M4.D, J2.pin22, Part1.Z_BTM_1B
  N19: M5.A, J3.pin5, Part1.E0_2B
  N20: M5.COMMON_1, J3.pin3
  N21: M5.C, J3.pin6, Part1.E0_2A
  N22: M5.B, J3.pin7, Part1.E0_1A
  N23: M5.COMMON_2, J3.pin4
  N24: M5.D, J3.pin8, Part1.E0_1B
  VIN: J1.pin1, Part1.5V/XMIN_ENDSTOP, Mod1.Vin, Mod2.Vin, Mod3.Vin, Mod4.Vin
  N25: J1.pin2, Part1.GND/XMIN_ENDSTOP, Mod1.-
  N26: J1.pin4, Part1.D3/XMIN_ENDSTOP, Mod1.S
  N27: J1.pin5, Part1.D2/XMAX_ENDSTOP, Mod4.S
  N28: J1.pin6, Part1.D14/YMIN_ENDSTOP, Mod3.S
  N29: J1.pin7, Part1.D15/YMAX_ENDSTOP, Mod2.S
  N30: Mod2.-, Mod3.-, Mod4.-
  N31: IC1.pin3, R1.Pin_1
  N32: IC1.pin5, IC1.pin12
  N33: IC1.pin6, IC1.pin9
  N34: IC1.pin7, R3.Pin_1, Q1.E
  N35: LED1.anode, R2.Pin_1
  N36: R1.Pin_0, Q1.B

notes:
  Photosensor Block
  Yellow = 5V
  Black = GND
  Black (x4) = Output
  Reel Block
  Green = Centre Pins (ignore)
  Black = Everything else...

custom parts:
  RAMPS 1.4 Shield for Arduino Mega 2560: This ia standard Ramps 1.4 shield which is also compatible with versions 1.5 and 1.6 of the Ramps board. This model is intended only for the breadboard view, as the schematic and PCB views are not entirely accurate.
  KY-010 Photo Interrupter Module: KY-010 Photo Interrupter Module, it will trigger a signal when light between the sensor's gap is blocked.
